// Logisim project Etapa1.circ as structural Verilog: 1 circuit, main circuit main
module main (
  input  A,
  input  B,
  input  E,
  input  C,
  input  D,
  output [8:0] SALIDA
);

  wire and_1_out, and_2_out, clock_1_out, multiplexer_1_out, not_1_out, not_2_out, undriven;
  wire [2:0] rom_1_data;

  Multiplexer #(.select(3)) multiplexer_1 (
    .in0(A), .in1(1'b0), .in2(B), .in3(E), .in4(C), .in5(1'b0), .in6(1'b0), .out(multiplexer_1_out),
    .sel(SALIDA[2:0]));  // open: in7
  and and_1 (and_1_out, D, and_2_out);
  not not_1 (not_1_out, and_1_out);
  Clock clock_1 (.out(clock_1_out));
  Counter #(.max('h6), .width(3)) counter_1 (
    .clr(undriven), .load(multiplexer_1_out), .up(1'b1), .count(not_1_out), .clk(clock_1_out),
    .D(rom_1_data), .Q(SALIDA[2:0]));  // open: carry
  and and_2 (and_2_out, SALIDA[0], SALIDA[1], not_2_out);
  ROM #(.addrWidth(3), .dataWidth(3)) rom_1 (.addr(SALIDA[2:0]), .data(rom_1_data));
  not not_2 (not_2_out, SALIDA[2]);
  not not_3 (SALIDA[8], 1'b0);

  assign SALIDA[7:3] = {5{1'b0}};

  // Notes on the sheet:
  //   ENTRADAS
  //   contents of rom_1 (hex, n*v repeats v):
  //   3 0 4 5
endmodule
