// Logisim project CLAA.circ as structural Verilog: 1 circuit, main circuit CLAA
module CLAA (
  input  B3,
  input  A3,
  input  B2,
  input  A2,
  input  B1,
  input  A1,
  input  B0,
  input  A0,
  input  Cin,
  output Cout,
  output S3,
  output S2,
  output S1,
  output S0
);

  wire and_1_out, and_2_out, and_3_out, and_4_out, circuitopg_1_c1, circuitopg_1_c2, circuitopg_1_c3,
       or_1_out, or_2_out, or_3_out, or_4_out, xor_1_out, xor_4_out, xor_6_out, xor_8_out;

  or or_1 (or_1_out, B3, A3);
  and and_1 (and_1_out, B3, A3);
  or or_2 (or_2_out, B2, A2);
  and and_2 (and_2_out, B2, A2);
  or or_3 (or_3_out, B1, A1);
  and and_3 (and_3_out, B1, A1);
  or or_4 (or_4_out, B0, A0);
  and and_4 (and_4_out, B0, A0);
  circuitoPG circuitopg_1 (
    .P3(or_1_out), .G3(and_1_out), .P2(or_2_out), .G2(and_2_out), .P1(or_3_out), .G1(and_3_out),
    .P0(or_4_out), .G0(and_4_out), .C0(Cin), .C4(Cout), .C3(circuitopg_1_c3), .C2(circuitopg_1_c2),
    .C1(circuitopg_1_c1));
  xor xor_1 (xor_1_out, B3, A3);
  xor xor_2 (S3, xor_1_out, circuitopg_1_c3);
  xor xor_3 (S2, circuitopg_1_c2, xor_4_out);
  xor xor_4 (xor_4_out, B2, A2);
  xor xor_5 (S1, circuitopg_1_c1, xor_6_out);
  xor xor_6 (xor_6_out, B1, A1);
  xor xor_7 (S0, Cin, xor_8_out);
  xor xor_8 (xor_8_out, B0, A0);

  // Notes on the sheet:
  //   ENTRADAS
  //   SALIDAS
endmodule
