// Logisim project CLAA24B.circ as structural Verilog: 1 circuit, main circuit CLAA24Bits
module CLAA24Bits (
  input  Cin,
  input  [23:0] A,
  input  [23:0] B,
  output [23:0] SUMA,
  output Cout
);

  wire CLAA03_cout, CLAA47_cout, CLAA811_cout, CLAA1215_cout, CLAA1619_cout;

  CLAA CLAA03 (
    .B3(B[3]), .A3(A[3]), .B2(B[2]), .A2(A[2]), .B1(B[1]), .A1(A[1]), .B0(B[0]), .A0(A[0]), .Cin(Cin),
    .Cout(CLAA03_cout), .S3(SUMA[3]), .S2(SUMA[2]), .S1(SUMA[1]), .S0(SUMA[0]));
  CLAA CLAA47 (
    .B3(B[7]), .A3(A[7]), .B2(B[6]), .A2(A[6]), .B1(B[5]), .A1(A[5]), .B0(B[4]), .A0(A[4]),
    .Cin(CLAA03_cout), .Cout(CLAA47_cout), .S3(SUMA[7]), .S2(SUMA[6]), .S1(SUMA[5]), .S0(SUMA[4]));
  CLAA CLAA811 (
    .B3(B[11]), .A3(A[11]), .B2(B[10]), .A2(A[10]), .B1(B[9]), .A1(A[9]), .B0(B[8]), .A0(A[8]),
    .Cin(CLAA47_cout), .Cout(CLAA811_cout), .S3(SUMA[11]), .S2(SUMA[10]), .S1(SUMA[9]), .S0(SUMA[8]));
  CLAA CLAA1215 (
    .B3(B[15]), .A3(A[15]), .B2(B[14]), .A2(A[14]), .B1(B[13]), .A1(A[13]), .B0(B[12]), .A0(A[12]),
    .Cin(CLAA811_cout), .Cout(CLAA1215_cout), .S3(SUMA[15]), .S2(SUMA[14]), .S1(SUMA[13]), .S0(SUMA[12]));
  CLAA CLAA1619 (
    .B3(B[19]), .A3(A[19]), .B2(B[18]), .A2(A[18]), .B1(B[17]), .A1(A[17]), .B0(B[16]), .A0(A[16]),
    .Cin(CLAA1215_cout), .Cout(CLAA1619_cout), .S3(SUMA[19]), .S2(SUMA[18]), .S1(SUMA[17]), .S0(SUMA[16]));
  CLAA CLAA2023 (
    .B3(B[23]), .A3(A[23]), .B2(B[22]), .A2(A[22]), .B1(B[21]), .A1(A[21]), .B0(B[20]), .A0(A[20]),
    .Cin(CLAA1619_cout), .Cout(Cout), .S3(SUMA[23]), .S2(SUMA[22]), .S1(SUMA[21]), .S0(SUMA[20]));

  // Other names for the same wires on the sheet: A03[3:0] = A[3:0]; A47[3:0] = A[7:4]; A811[3:0] = A[11:8];
  //   A1215[3:0] = A[15:12]; A1619[3:0] = A[19:16]; A2023[3:0] = A[23:20]; B03[3:0] = B[3:0]; B47[3:0] = B[7:4];
  //   B811[3:0] = B[11:8]; B1215[3:0] = B[15:12]; B1619[3:0] = B[19:16]; B2023[3:0] = B[23:20]; S03[3:0] = SUMA[3:0];
  //   S47[3:0] = SUMA[7:4]; S811[3:0] = SUMA[11:8]; S1215[3:0] = SUMA[15:12]; S1619[3:0] = SUMA[19:16];
  //   S2023[3:0] = SUMA[23:20]

  // Notes on the sheet:
  //   ENTRADAS
  //   SALIDAS
endmodule
