// Logisim project Etapa2.circ as structural Verilog: 1 circuit, main circuit main
module main (
  input  A,
  input  E,
  input  B,
  input  C,
  input  D,
  input  in_6,
  output [8:0] SALIDA
);

  wire and_1_out, and_2_out, clock_1_out, multiplexer_1_out, not_1_out, not_2_out, not_4_out, not_5_out,
       or_1_out;
  wire [2:0] claa24bits_1_suma, claa24bits_1_suma_2, claa24bits_1_suma_3, claa24bits_1_suma_4,
       claa24bits_1_suma_5, claa24bits_1_suma_6, claa24bits_1_suma_7, claa24bits_1_suma_8;
  wire [7:0] rom_1_data;
  wire [8:8] not_3_out;
  wire [23:0] bit_extender_1_out, bit_extender_2_out;

  Multiplexer #(.select(3)) multiplexer_1 (
    .in0(A), .in1(1'b0), .in2(B), .in3(E), .in4(C), .in5(1'b0), .in6(not_1_out), .in7(1'b0),
    .out(multiplexer_1_out), .sel(SALIDA[2:0]));
  not not_1 (not_1_out, 1'b0);
  and and_1 (and_1_out, D, and_2_out);
  Clock clock_1 (.out(clock_1_out));
  or or_1 (or_1_out, not_5_out, multiplexer_1_out);
  not not_2 (not_2_out, and_1_out);
  not not_3 (not_3_out[8], 1'b0);
  ROM #(.addrWidth(4)) rom_1 (.addr({SALIDA[8], SALIDA[2:0]}), .data(rom_1_data));
  Counter #(.max('h1ff), .width(9)) counter_1 (
    .load(or_1_out), .up(1'b1), .count(not_2_out), .clk(clock_1_out),
    .D({not_3_out[8], {5{1'b0}}, claa24bits_1_suma}), .Q(SALIDA));  // open: clr, carry
  and and_2 (and_2_out, SALIDA[0], SALIDA[1], not_4_out);
  not not_4 (not_4_out, SALIDA[2]);
  not not_5 (not_5_out, SALIDA[8]);
  assign bit_extender_1_out = {{15{SALIDA[8]}}, SALIDA};  // Bit_Extender bit_extender_1
  assign bit_extender_2_out = {{16{rom_1_data[7]}}, rom_1_data};  // Bit_Extender bit_extender_2
  CLAA24Bits claa24bits_1 (
    .Cin(in_6), .A(bit_extender_1_out), .B(bit_extender_2_out),
    .SUMA({claa24bits_1_suma_8, claa24bits_1_suma_7, claa24bits_1_suma_6, claa24bits_1_suma_5, claa24bits_1_suma_4, claa24bits_1_suma_3, claa24bits_1_suma_2, claa24bits_1_suma}));  // open: Cout

  // Notes on the sheet:
  //   ENTRADAS
  //   Estado actual
  //   Load
  //   contents of rom_1 (hex, n*v repeats v):
  //   8*0 3 0 2 2 fc 0 fa
  //   Bits de direccionamiento ROM
endmodule
