// Logisim project FA.circ as structural Verilog: 1 circuit, main circuit FA
module FA (
  input  A,
  input  B,
  input  Cin,
  output S,
  output Cout
);

  wire and_1_out, and_2_out, and_3_out;

  ExactlyOne xor_1 (.out(S), .in0(A), .in1(B), .in2(Cin));
  and and_1 (and_1_out, Cin, B);
  and and_2 (and_2_out, Cin, A);
  and and_3 (and_3_out, B, A);
  or or_1 (Cout, and_1_out, and_2_out, and_3_out);
endmodule
