// Logisim project carrys.circ as structural Verilog: 1 circuit, main circuit main
module main (
  input  Cin,
  input  [3:0] B,
  input  [3:0] A,
  output GG,
  output Cout,
  output PG
);

  wire C1_cim1, C2_cim1, C3_cim1, fa_1_s;

  generadorPG C1 (.Ci(Cin), .Ai(A[0]), .Bi(B[0]), .Cim1(C1_cim1));  // open: Gi, Pi
  generadorPG C2 (.Ci(C1_cim1), .Ai(A[1]), .Bi(B[1]), .Cim1(C2_cim1));  // open: Gi, Pi
  generadorPG C3 (.Ci(C2_cim1), .Ai(A[2]), .Bi(B[2]), .Cim1(C3_cim1));  // open: Gi, Pi
  generadorPG C4 (.Ci(C3_cim1), .Ai(A[3]), .Bi(B[3]), .Gi(GG), .Cim1(Cout), .Pi(PG));
  FA fa_1 (.A(A[0]), .B(B[0]), .Cin(Cin), .S(fa_1_s));  // open: Cout
endmodule
