// Logisim project carrys.circ as structural Verilog: 1 circuit, main circuit main
module main (
);

  wire generadorpg_1_cim1, generadorpg_2_cim1, generadorpg_3_cim1, generadorpg_4_cim1;

  generadorPG generadorpg_1 (.Cim1(generadorpg_1_cim1));  // open: Ci, Ai, Bi, Gi, Pi
  generadorPG generadorpg_2 (.Ci(generadorpg_1_cim1), .Cim1(generadorpg_2_cim1));  // open: Ai, Bi, Gi, Pi
  generadorPG generadorpg_3 (.Ci(generadorpg_2_cim1), .Cim1(generadorpg_3_cim1));  // open: Ai, Bi, Gi, Pi
  generadorPG generadorpg_4 (.Ci(generadorpg_3_cim1), .Cim1(generadorpg_4_cim1));  // open: Ai, Bi, Gi, Pi
  generadorPG generadorpg_5 (.Ci(generadorpg_4_cim1));  // open: Ai, Bi, Gi, Cim1, Pi

  // Notes on the sheet:
  //   C1
  //   C2
  //   C3
  //   C4
  //   C5
endmodule
