// Logisim project generador.circ as structural Verilog: 1 circuit, main circuit generadorPG
module generadorPG (
  input  Ci,
  input  Ai,
  input  Bi,
  output Gi,
  output Cim1,
  output Pi
);

  wire and_2_out;

  and and_1 (Gi, Ai, Bi);
  or or_1 (Pi, Ai, Bi);
  and and_2 (and_2_out, Ci, Pi);
  or or_2 (Cim1, Gi, and_2_out);
endmodule
